# Fritzing sketch BigBreadBoard.fzz  mid term (saved by Fritzing 0.9.4)
breadboards: 3

parts:
  Breadboard4 = Breadboard Split Power
  Breadboard5 = Breadboard Split Power  # not connected
  Teensy_3_1 = Teensy 3.1
  U1 = ENCODER_RGB [package=encoder_led_2]
  WIZ820io1 = WIZ820io [part_number=WIZ820io]
  OLED_I2C1 = OLED 128x64 I2C Monochrome Display  # not connected
  M1 = BMP280  # not connected
  P1 = S1133 Si Photodiode [package="8mm Ceramic [THT]"]
  R2 = Resistor [tolerance=±5% resistance=220 package="2512 [SMD]"]
  R3 = Resistor [tolerance=±5% resistance=220 package="2512 [SMD]"]
  R4 = Resistor [tolerance=±5% resistance=220 package="2512 [SMD]"]
  S3 = Pushbutton [package="[THT]"]
  S4 = Pushbutton [package="[THT]"]
  R5 = Resistor [tolerance=±5% resistance=220 package="2512 [SMD]"]

nets:
  N1: Breadboard4.pin3Z, Breadboard4.pin20Z, Teensy_3_1.A3/D17, WIZ820io1.GND, P1.cathode, R2.Pin_1, R3.Pin_1, R4.Pin_0
  N2: Breadboard4.pin4Y, P1.anode
  N3: Breadboard4.pin21Y, WIZ820io1.VIN, S3.Pin_1, S3.Pin_2
  N4: Teensy_3_1.D5, R3.Pin_0, S3.Pin_3, S3.Pin_4
  N5: Teensy_3_1.D6, R2.Pin_0, S4.Pin_3, S4.Pin_4
  N6: Teensy_3_1.D7, WIZ820io1.nRESET
  N7: Teensy_3_1.D10, WIZ820io1.nSS
  N8: Teensy_3_1.D11, WIZ820io1.MISO
  N9: Teensy_3_1.D12, WIZ820io1.MOSI
  N10: Teensy_3_1.D13, WIZ820io1.SCLK
  N11: U1.SW, R5.Pin_1
  N12: S4.Pin_1, S4.Pin_2

custom parts:
  Breadboard Split Power: A custom 6 pin per group power supply strip where the top row (ground) is all bussed together and the bottom row (+V) is split in two groups of 12 pins. This version is modified to be a loadable part and was rescaled to be on the standard 1px = 1thou grid with the size set in inches
  ENCODER_RGB: SparkFun RGB rotary Encoder
  BMP280: Temperature Humidity Barometric presure Sensor, I2C
  Pushbutton: A generic pushbutton.
  Pushbutton: A generic pushbutton.
